# Fritzing sketch Reciever board (saved by Fritzing 0.9.3b)
circuit board: 2.9cm x 5cm
breadboards: 1

parts:
  Nano = Arduino Nano (Rev3.0)
  Green = LED - 5mm [color="Green (570nm)" package="5 mm [THT]"]
  White = LED - 5mm [color="White (4500K)" package="5 mm [THT]"]
  R1 = Resistor [tolerance=±5% resistance=220 package=THT]
  Ultrasonic = hc-sr04
  Reed = Reed switch [package=THT]
  +6v = Battery
  RF_Reciever = XD-RF-5V [package=THT]

nets:
  GND: Nano.GND, R1.Pin_1, Ultrasonic.GND, +6v.-, RF_Reciever.GND
  N1: Nano.D3, RF_Reciever.DATA#1
  N2: Nano.D5, Ultrasonic.Echo
  N3: Nano.D6, Ultrasonic.Trig
  N4: Nano.D10, White.anode
  N5: Nano.D12/MISO, Green.anode
  N6: Nano.VIN, Reed.pin_1
  VCC: Nano.5V, Ultrasonic.VCC, RF_Reciever.VCC
  N7: Green.cathode, White.cathode, R1.Pin_0
  N8: Reed.pin_2, +6v.+

notes:
  WP Rx V1.0
  David Cai

custom parts:
  XD-RF-5V: This is 433Mhz RF transmitter with receiver kit for Arduino ARM MCU wireless Application environment: Remote control switch, receiver module, motorcycles, automobile anti-theft products, home security products, electric doors, shutter doors, windows, remote control socket, remote control LED, remote audio remote control electric doors, garage door remote control, remote control retractable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
